# Fritzing sketch LCD-Display am Raspberry Pi (saved by Fritzing 0.7.7b)
breadboards: 1

parts:
  Raspberry_Pi1 = Raspberry Pi (Model B)
  MCP1 = MCP23016 [package="DIP (Dual Inline) [THT]"]
  R1 = Resistor [tolerance=±5% resistance=3.9k package=THT]
  C1 = Ceramic Capacitor [capacitance=10pF package="100 mil [THT, multilayer]"]
  Nokia_5110_LCD_Module1 = Nokia5110LCDModule
  R2 = Resistor [tolerance=±5% resistance=10k package=THT]
  R3 = Resistor [tolerance=±5% resistance=10k package=THT]
  R4 = Resistor [tolerance=±5% resistance=10k package=THT]
  R5 = Resistor [tolerance=±5% resistance=10k package=THT]
  R13 = Resistor [tolerance=±5% resistance=1k package=THT]  # not connected

nets:
  5V: Raspberry_Pi1.5V, MCP1.VDD, R1.Pin_0, Nokia_5110_LCD_Module1.Vcc
  N1: Raspberry_Pi1.SDA, MCP1.SDA
  N2: Raspberry_Pi1.SCL, MCP1.SCL
  N3: Raspberry_Pi1.GND, MCP1.A0, MCP1.A1, MCP1.A2, MCP1.VSS#18, Nokia_5110_LCD_Module1.Grnd, Nokia_5110_LCD_Module1.SCE
  N4: MCP1.VSS#7, C1.1
  N5: MCP1.CLK, R1.Pin_1, C1.0
  N6: MCP1.GP0.4, R5.Pin_1
  N7: MCP1.GP0.5, R4.Pin_1
  N8: MCP1.GP0.6, R3.Pin_1
  N9: MCP1.GP0.7, R2.Pin_1
  N10: Nokia_5110_LCD_Module1.RST, R2.Pin_0
  N11: Nokia_5110_LCD_Module1.D/C, R3.Pin_0
  N12: Nokia_5110_LCD_Module1.6_DN_(MOSI), R4.Pin_0
  N13: Nokia_5110_LCD_Module1.SCLK, R5.Pin_0

notes:
  Statt blauer Drähte
  können 1k Widerstände
  benutzt werden

custom parts:
  Raspberry Pi (Model B): Raspberry Pi Single-board Computer, Model B
  MCP23016: An I2C BUS 16 bit I/O expander.
  : Nokia 5110 LCD with 8 pin. It's a 45mm*45mm module part. Description: The Nokia 5110 is a basic graphic LCD screen for lots of applications. It was originally intended for as a cell phone screen. This one is mounted on an easy to solder PCB. It uses the PCD8544 controller. The PCD8544 is a low power CMOS LCD controller/driver, designed to drive a graphic display of 48 rows and 84 columns. All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
